// Digital circuit Capstone_Circuit.dig as structural Verilog
module Capstone_Circuit (
  input  L,
  input  R,
  input  CLK,
  output H,
  output C
);

  wire and_1_out, and_2_out, and_3_out, and_4_out, and_5_out, and_6_out, and_7_out, and_8_out, J0, J1, J2,
       K0, K1, K2, L_t, Q0, Q0_t, Q1, Q1_t, Q2, Q2_t, R_t;

  not not_1 (L_t, L);
  not not_2 (R_t, R);
  and and_1 (and_1_out, Q1, Q0);
  and and_2 (and_2_out, R, Q0_t);
  and and_3 (and_3_out, Q1_t, R);
  and and_4 (and_4_out, R, Q0_t);
  and and_5 (and_5_out, Q2, Q0);
  and and_6 (and_6_out, Q0_t, R);
  and and_7 (and_7_out, R, Q0_t);
  or or_1 (J0, R, L);
  and and_8 (and_8_out, R, Q2_t);
  or or_2 (J2, and_1_out, and_2_out, and_3_out);
  or or_3 (K2, and_4_out, L);
  or or_4 (J1, and_5_out, and_6_out);
  or or_5 (K1, and_7_out, Q0);
  or or_6 (K0, Q2, and_8_out, Q1);
  JK_FF JK2 (.J(J2), .C(CLK), .K(K2), .Q(Q2), .nQ(Q2_t));
  JK_FF JK1 (.J(J1), .C(CLK), .K(K1), .Q(Q1), .nQ(Q1_t));
  JK_FF JK0 (.J(J0), .C(CLK), .K(K0), .Q(Q0), .nQ(Q0_t));
  and and_9 (H, Q2_t, Q1_t);
  and and_10 (C, Q2, Q1_t);
endmodule
