// Digital circuit addr_gen.dig as structural Verilog
module addr_gen (
  input  [3:0] data__bus,
  input  clk,
  input  reset,
  input  use__pc,
  input  load__mar,
  output [3:0] addr__bus
);

  wire [3:0] mar, pc;

  program_ctr program_ctr_1 (.enable(use__pc), .reset(reset), .clk(clk), .q(pc));
  four_bit_reg four_bit_reg_1 (.d(data__bus), .enable(load__mar), .clk(clk), .reset(reset), .q(mar));
  four_bit_mux four_bit_mux_1 (.a(pc), .b(mar), .sel(use__pc), .y(addr__bus));
endmodule
