// Digital circuit brainless.dig as structural Verilog
module brainless (
  input  [3:0] addr__bus,
  input  [3:0] data__in,
  input  arith,
  input  invert,
  input  pass,
  input  load__acc,
  input  acc__to__db,
  input  read,
  input  write,
  input  clk,
  input  reset,
  output [3:0] accum,
  output [3:0] alu__out,
  output [3:0] data__bus
);

  wire [3:0] data__mux_y, program_ram_1_data__out;

  alu accumulator (
    .invert(invert), .a(data__bus), .b(accum), .arith(arith), .cin(1'b0), .pass(pass), .y(alu__out));  // open: cout, overfl
  four_bit_reg accum__mux (.d(alu__out), .enable(load__acc), .clk(clk), .reset(reset), .q(accum));
  four_bit_mux four_bit_mux_1 (.a(data__mux_y), .b(accum), .sel(acc__to__db), .y(data__bus));
  program_ram program_ram_1 (
    .addr(addr__bus), .data__in(data__bus), .write(write), .clk(clk), .data__out(program_ram_1_data__out));
  four_bit_mux data__mux (.a(data__in), .b(program_ram_1_data__out), .sel(read), .y(data__mux_y));
endmodule
