// Digital circuit controller.dig as structural Verilog
module controller (
  input  clk,
  input  reset,
  input  [3:0] data__bus,
  input  load__ir,
  output [9:0] control
);

  wire [1:0] step__reg;
  wire [3:0] instr;
  wire [13:10] rom__out;

  four_bit_reg instruction_reg (.d(data__bus), .enable(load__ir), .clk(clk), .reset(reset), .q(instr));
  two_bit_reg step_reg (.d(rom__out[13:12]), .enable(1'b1), .clk(clk), .reset(reset), .q(step__reg));
  ROM #(.AddrBits(6), .Bits(14)) microcode_ROM (.A({instr, step__reg}), .sel(1'b1), .D({rom__out, control}));

  // Other names for the same wires on the sheet: rom__out[9:0] = control

  // Notes on the sheet:
  //   contents of microcode_ROM (hex, n*v repeats v):
  //   1205,234,0,0,1205,294,0,0,1205,1000,0,0,1205,0,0,0,1205,0,0,0
  //   ,1205,0,0,0,1205,0,0,0,1205,0,0,3fff
endmodule
